// Logisim project Lab1_1.circ as structural Verilog: 1 circuit, main circuit main
module main (
  input  pin_1,
  input  pin_2
);

  wire and_1_out;

  and and_1 (and_1_out, pin_1, pin_2);
  LED led_1 (.in(and_1_out));

  // Notes on the sheet:
  //   AND
  //   output (LED)
endmodule
