// Logisim project Lab1_2.circ as structural Verilog: 1 circuit, main circuit main
module main (
  input  pin_1
);

  wire not_1_out;

  not not_1 (not_1_out, pin_1);
  LED led_1 (.in(not_1_out));

  // Notes on the sheet:
  //   NOT
  //   output (LED)
endmodule
