// Logisim project Lab1_FullAdder.circ as structural Verilog: 1 circuit, main circuit main
module main (
  input  carry_in,
  input  pin_1,
  input  pin_2
);

  wire and_1_out, and_2_out, or_1_out, xor_1_out, xor_2_out;

  xor xor_1 (xor_1_out, pin_1, pin_2);
  and and_1 (and_1_out, pin_1, pin_2);
  xor xor_2 (xor_2_out, carry_in, xor_1_out);
  and and_2 (and_2_out, carry_in, xor_1_out);
  LED led_1 (.in(xor_2_out));
  or or_1 (or_1_out, and_2_out, and_1_out);
  LED led_2 (.in(or_1_out));

  // Notes on the sheet:
  //   XOR
  //   AND
  //   XOR
  //   AND
  //   OR
  //   sum output (LED)
  //   carry output (LED)
endmodule
