// Logisim project Lab1_HalfAdder.circ as structural Verilog: 1 circuit, main circuit main
module main (
  input  pin_1,
  input  pin_2
);

  wire and_1_out, xor_1_out;

  xor xor_1 (xor_1_out, pin_1, pin_2);
  and and_1 (and_1_out, pin_1, pin_2);
  LED led_1 (.in(xor_1_out));
  LED led_2 (.in(and_1_out));

  // Notes on the sheet:
  //   XOR
  //   AND
  //   sum output (LED)
  //   carry output (LED)
endmodule
