// Logisim project 4bitAdder.circ as structural Verilog: 1 circuit, main circuit main
module main (
  input  Input_A1,
  input  Input_B1,
  input  Input_A2,
  input  Input_B2,
  input  Input_A3,
  input  Input_B3,
  input  Input_A4,
  input  Input_B4,
  output sum_1,
  output carry_1,
  output sum_2,
  output carry_2,
  output sum_3,
  output carry_3,
  output sum_4,
  output carry_4
);

  wire AND_2_out, AND_3_out, AND_4_out, AND_5_out, AND_6_out, AND_7_out, XOR_2_out, XOR_3_out, XOR_4_out;

  xor XOR (sum_1, Input_A1, Input_B1);
  and AND (carry_1, Input_A1, Input_B1);
  xor XOR_2 (XOR_2_out, Input_A2, Input_B2);
  and AND_2 (AND_2_out, Input_A2, Input_B2);
  xor XOR_3 (XOR_3_out, Input_A3, Input_B3);
  and AND_3 (AND_3_out, Input_A3, Input_B3);
  xor XOR_4 (XOR_4_out, Input_A4, Input_B4);
  and AND_4 (AND_4_out, Input_A4, Input_B4);
  xor XOR_5 (sum_2, carry_1, XOR_2_out);
  and AND_5 (AND_5_out, carry_1, XOR_2_out);
  xor XOR_6 (sum_3, carry_2, XOR_3_out);
  and AND_6 (AND_6_out, carry_2, XOR_3_out);
  xor XOR_7 (sum_4, carry_3, XOR_4_out);
  and AND_7 (AND_7_out, carry_3, XOR_4_out);
  or OR (carry_2, AND_5_out, AND_2_out);
  or OR_2 (carry_3, AND_6_out, AND_3_out);
  or OR_3 (carry_4, AND_7_out, AND_4_out);
endmodule
