// Logisim project dFlipFlop.circ as structural Verilog: 1 circuit, main circuit main
module main (
  input  data,
  output Q,
  output Q_prime
);

  wire clock_1_out, NAND_2_out, NAND_out, not_1_out;

  Clock clock_1 (.out(clock_1_out));
  not not_1 (not_1_out, data);
  nand NAND (NAND_out, not_1_out, clock_1_out);
  nand NAND_2 (NAND_2_out, clock_1_out, data);
  nor NOR (Q, NAND_out, Q_prime);
  nor NOR_2 (Q_prime, Q, NAND_2_out);

  // Notes on the sheet:
  //   clock
  //   NOT
endmodule
