// Logisim project storingBitsWithFlipFlops.circ as structural Verilog: 1 circuit, main circuit main
module main (
  input  set,
  input  reset,
  output Q,
  output Q_prime
);

  nor NOR (Q, set, Q_prime);
  nor NOR_2 (Q_prime, Q, reset);
endmodule
