// Logisim project JKCommon.circ as structural Verilog: 1 circuit, main circuit main
module main (
  input  in_1,
  output out_2,
  output out_3,
  output out_4
);

  wire clock_1_out;

  J_K_Flip_Flop j_k_ff_1 (.J(in_1), .K(in_1), .clk(clock_1_out), .Q(out_2));  // open: Qn, preset, reset
  Clock clock_1 (.out(clock_1_out));
  J_K_Flip_Flop j_k_ff_2 (.J(in_1), .K(in_1), .clk(clock_1_out), .Q(out_3));  // open: Qn, preset, reset
  J_K_Flip_Flop j_k_ff_3 (.J(in_1), .K(in_1), .clk(clock_1_out), .Q(out_4));  // open: Qn, preset, reset
endmodule
