// Logisim project JKRippleCounter.circ as structural Verilog: 1 circuit, main circuit main
module main (
  input  in_1,
  input  in_2,
  output out_3,
  output out_4,
  output out_5
);

  wire clock_1_out;

  J_K_Flip_Flop j_k_ff_1 (.J(in_1), .K(in_1), .clk(out_4), .Q(out_3), .reset(in_2));  // open: Qn, preset
  Clock clock_1 (.out(clock_1_out));
  J_K_Flip_Flop j_k_ff_2 (.J(in_1), .K(in_1), .clk(out_5), .Q(out_4), .reset(in_2));  // open: Qn, preset
  J_K_Flip_Flop j_k_ff_3 (.J(in_1), .K(in_1), .clk(clock_1_out), .Q(out_5), .reset(in_2));  // open: Qn, preset
endmodule
