// Logisim project question11.circ as structural Verilog: 1 circuit, main circuit main
module main (
  input  in_1,
  input  in_2,
  input  in_3
);

  wire and_1_out, and_2_out, and_3_out, and_4_out, clock_1_out, d_ff_1_q, d_ff_1_qn, d_ff_2_qn, not_1_out,
       or_1_out, or_2_out;

  and and_1 (and_1_out, in_3, in_1);
  Clock clock_1 (.out(clock_1_out));
  not not_1 (not_1_out, in_1);
  or or_1 (or_1_out, and_1_out, and_2_out);
  D_Flip_Flop d_ff_1 (.D(or_1_out), .clk(clock_1_out), .Q(d_ff_1_q), .Qn(d_ff_1_qn));  // open: preset, reset
  buf and_2 (and_2_out, not_1_out);  // AND_Gate
  LED led_1 (.in(d_ff_1_qn));
  and and_3 (and_3_out, d_ff_1_q, in_1);
  and and_4 (and_4_out, not_1_out, in_2);
  or or_2 (or_2_out, and_3_out, and_4_out);
  D_Flip_Flop d_ff_2 (.D(or_2_out), .clk(clock_1_out), .Qn(d_ff_2_qn));  // open: Q, preset, reset
  LED led_2 (.in(d_ff_2_qn));
endmodule
